# Fritzing sketch iLED (saved by Fritzing 0.9.3b)
breadboards: 1

parts:
  LED1 = LED - 5mm [color="Green (560nm)" package="5 mm [THT]"]
  LED2 = LED - 5mm [color="Red (635nm)" package="5 mm [THT]"]
  U1 = NodeMCU V1.0

nets:
  N1: LED1.cathode, LED2.cathode, U1.GND
  N2: LED1.anode, U1.D1
  N3: LED2.anode, U1.D0

custom parts:
  NodeMCU V1.0: ESP8266 based NodeMCU
